# Fritzing sketch schema (saved by Fritzing 0.9.3b)

parts:
  Bauteil1 = Arduino Nano (Rev3.0)
  U1 = 16-Channel Relay Module [package=relay-16ch]
  JP1 = Header 3 [package=molex-1x3_lock]
  U2 = FS1000A - 433Mhz RF Transmitter [package=THT]

nets:
  GND: Bauteil1.D0/RX, Bauteil1.RESET, Bauteil1.GND, Bauteil1.D2, Bauteil1.VIN, U1.OUT_GND, JP1.3, U2.DATA
  N1: Bauteil1.D3, U1.IN14
  N2: Bauteil1.D4, U1.IN13
  N3: Bauteil1.D5, U1.IN12
  N4: Bauteil1.D6, U1.IN11
  N5: Bauteil1.D7, U1.IN10
  N6: Bauteil1.D8, U1.IN9
  N7: Bauteil1.D9, U1.IN1
  N8: Bauteil1.D10, U1.IN2
  N9: Bauteil1.D11/MOSI, U1.IN3
  N10: Bauteil1.D12/MISO, U1.IN4
  N11: Bauteil1.5V, Bauteil1.A7, JP1.1
  N12: Bauteil1.A6, U1.IN15
  N13: Bauteil1.A5, U1.IN8
  N14: Bauteil1.A4, U1.IN7
  N15: Bauteil1.A3, U1.IN6
  N16: Bauteil1.A2, Bauteil1.A1, Bauteil1.A0, Bauteil1.AREF, U1.IN5, U1.IN16, JP1.2

notes:
  1-Wire Connector
  5V
  Data
  GND
  N.C.

custom parts:
  16-Channel Relay Module: 16 channel relay module
  FS1000A - 433Mhz RF Transmitter: This is 433Mhz RF transmitter with receiver kit for Arduino ARM MCU wireless Application environment: Remote control switch, receiver module, motorcycles, automobile anti-theft products, home security products, electric doors, shutter doors, windows, remote control socket, remote control LED, remote audio remote control electric doors, garage door remote control, remote control retractable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
